// Logisim project risk16.circ as structural Verilog: 14 circuits, main circuit IF
module IF (
  input  [15:0] PC,
  output [15:0] PC_1,
  output [2:0] OP,
  output [2:0] rA,
  output [2:0] rB,
  output [3:0] out_6,
  output [2:0] rC,
  output [15:0] PC_2
);

  ROM #(.addrWidth(16), .dataWidth(16)) rom_1 (.addr(PC), .data({OP, rA, rB, out_6, rC}), .sel(1'b1));
  Adder #(.width(16)) adder_1 (.a(PC), .b(16'h1), .out(PC_1));  // open: cin, cout

  assign PC_2 = PC;

  // Notes on the sheet:
  //   contents of rom_1 (hex, n*v repeats v):
  //   280a 2400 0 0 c506 0 0 2481 c07b 0 0 e071
endmodule

module ID (
  input  [2:0] OP,
  input  [2:0] rA,
  input  [2:0] rB,
  input  [3:0] in_4,
  input  [2:0] rC,
  input  [15:0] PC,
  input  [15:0] TGT_Value,
  input  [2:0] TGT_Adress,
  input  WErf,
  output [2:0] OP_2,
  output [2:0] rT,
  output [15:0] PC_2,
  output [15:0] OPERAND0,
  output [15:0] OPERAND2,
  output [15:0] OPERAND1
);

  wire ctl6_1_muxop0, ctl6_1_muxs2;
  wire [2:0] multiplexer_1_out;

  CTL7 ctl7_1 (.OP(OP), .rA(rA), .OP_2(OP_2), .rT(rT));
  CTL6 ctl6_1 (.OP(OP_2), .MUXs2(ctl6_1_muxs2), .MUXop0(ctl6_1_muxop0));
  Multiplexer #(.width(3), .disabled(0), .enable("false")) multiplexer_1 (
    .in0(rA), .in1(rC), .out(multiplexer_1_out), .sel(ctl6_1_muxs2));
  Multiplexer #(.width(16), .disabled(0), .enable("false")) multiplexer_2 (
    .in0({{10{in_4[3]}}, in_4[2:0], rC}), .in1({rB, in_4, rC, {6{1'b0}}}), .out(OPERAND0), .sel(ctl6_1_muxop0));
  REGISTER_FILE register_file_1 (
    .TGT_2(TGT_Adress), .SRC1(rB), .SRC2(multiplexer_1_out), .TGT(TGT_Value), .WErf(WErf), .SRC2_2(OPERAND2),
    .SRC1_2(OPERAND1));

  assign PC_2 = PC;

  // Notes on the sheet:
  //   Sign-Ext-7
  //   Left-Shift-6
endmodule

module REGISTER_FILE (
  input  [15:0] TGT,
  input  [2:0] TGT_2,
  input  [2:0] SRC1,
  input  [2:0] SRC2,
  input  WErf,
  output [15:0] SRC2_2,
  output [15:0] SRC1_2
);

  wire clock_1_out, demultiplexer_1_out1, demultiplexer_1_out2, demultiplexer_1_out3, demultiplexer_1_out4,
       demultiplexer_1_out5, demultiplexer_1_out6, demultiplexer_1_out7;
  wire [15:0] multiplexer_1_out, multiplexer_2_out, multiplexer_3_out, multiplexer_4_out, multiplexer_5_out,
       multiplexer_6_out, multiplexer_7_out, register_1_q, register_2_q, register_3_q, register_4_q,
       register_5_q, register_6_q, register_7_q;

  Demultiplexer #(.select(3), .disabled(0), .enable("false")) demultiplexer_1 (
    .out1(demultiplexer_1_out1), .out2(demultiplexer_1_out2), .out3(demultiplexer_1_out3),
    .out4(demultiplexer_1_out4), .out5(demultiplexer_1_out5), .out6(demultiplexer_1_out6),
    .out7(demultiplexer_1_out7), .in(WErf), .sel(TGT_2));  // open: out0
  Register #(.width(16), .trigger("falling")) register_1 (
    .D(multiplexer_1_out), .en(1'b1), .Q(register_1_q), .clk(clock_1_out));  // open: clr
  Multiplexer #(.width(16), .disabled(0), .enable("false")) multiplexer_1 (
    .in0(register_1_q), .in1(TGT), .out(multiplexer_1_out), .sel(demultiplexer_1_out1));
  Register #(.width(16), .trigger("falling")) register_2 (
    .D(multiplexer_2_out), .en(1'b1), .Q(register_2_q), .clk(clock_1_out));  // open: clr
  Multiplexer #(.width(16), .disabled(0), .enable("false")) multiplexer_2 (
    .in0(register_2_q), .in1(TGT), .out(multiplexer_2_out), .sel(demultiplexer_1_out2));
  Register #(.width(16), .trigger("falling")) register_3 (
    .D(multiplexer_3_out), .en(1'b1), .Q(register_3_q), .clk(clock_1_out));  // open: clr
  Multiplexer #(.width(16), .disabled(0), .enable("false")) multiplexer_3 (
    .in0(register_3_q), .in1(TGT), .out(multiplexer_3_out), .sel(demultiplexer_1_out3));
  Multiplexer #(.width(16), .disabled(0), .enable("false")) multiplexer_4 (
    .in0(register_4_q), .in1(TGT), .out(multiplexer_4_out), .sel(demultiplexer_1_out4));
  Register #(.width(16), .trigger("falling")) register_4 (
    .D(multiplexer_4_out), .en(1'b1), .Q(register_4_q), .clk(clock_1_out));  // open: clr
  Multiplexer #(.width(16), .disabled(0), .enable("false")) multiplexer_5 (
    .in0(register_5_q), .in1(TGT), .out(multiplexer_5_out), .sel(demultiplexer_1_out5));
  Register #(.width(16), .trigger("falling")) register_5 (
    .D(multiplexer_5_out), .en(1'b1), .Q(register_5_q), .clk(clock_1_out));  // open: clr
  Multiplexer #(.width(16), .disabled(0), .enable("false")) multiplexer_6 (
    .in0(register_6_q), .in1(TGT), .out(multiplexer_6_out), .sel(demultiplexer_1_out6));
  Register #(.width(16), .trigger("falling")) register_6 (
    .D(multiplexer_6_out), .en(1'b1), .Q(register_6_q), .clk(clock_1_out));  // open: clr
  Multiplexer #(.width(16), .disabled(0), .enable("false")) multiplexer_7 (
    .in0(register_7_q), .in1(TGT), .out(multiplexer_7_out), .sel(demultiplexer_1_out7));
  Register #(.width(16), .trigger("falling")) register_7 (
    .D(multiplexer_7_out), .en(1'b1), .Q(register_7_q), .clk(clock_1_out));  // open: clr
  Clock clock_1 (.out(clock_1_out));
  Multiplexer #(.select(3), .width(16), .disabled(0), .enable("false")) multiplexer_8 (
    .in0({16{1'b0}}), .in1(register_1_q), .in2(register_2_q), .in3(register_3_q), .in4(register_4_q),
    .in5(register_5_q), .in6(register_6_q), .in7(register_7_q), .out(SRC1_2), .sel(SRC1));
  Multiplexer #(.select(3), .width(16), .enable("false")) multiplexer_9 (
    .in0({16{1'b0}}), .in1(register_1_q), .in2(register_2_q), .in3(register_3_q), .in4(register_4_q),
    .in5(register_5_q), .in6(register_6_q), .in7(register_7_q), .out(SRC2_2), .sel(SRC2));
endmodule

module CTL7 (
  input  [2:0] OP,
  input  [2:0] rA,
  output [2:0] OP_2,
  output [2:0] rT
);

  wire and_1_out, xor_1_out;

  xor xor_1 (xor_1_out, OP[0], OP[1]);
  and and_1 (and_1_out, xor_1_out, OP[2]);
  Multiplexer #(.width(3), .disabled(0), .enable("false")) multiplexer_1 (
    .in0(rA), .in1(3'b000), .out(rT), .sel(and_1_out));

  assign OP_2 = OP;
endmodule

module CTL6 (
  input  [2:0] OP,
  output MUXs2,
  output MUXop0
);

  wire not_1_out, not_2_out, not_3_out;

  and and_1 (MUXs2, not_2_out, not_1_out);
  not not_1 (not_1_out, OP[0]);
  not not_2 (not_2_out, OP[2]);
  not not_3 (not_3_out, OP[2]);
  and and_2 (MUXop0, not_3_out, OP[1], OP[0]);
endmodule

module EX (
  input  [2:0] OP,
  input  [2:0] rT,
  input  [15:0] PC,
  input  [15:0] OPERAND0,
  input  [15:0] OPERAND2,
  input  [15:0] OPERAND1,
  output [1:0] MUXpc,
  output [15:0] MUXpc_v1,
  output [15:0] MUXpc_v2,
  output [2:0] OP_2,
  output [2:0] rT_2,
  output [15:0] PC_2,
  output [15:0] STORE_DATA,
  output [15:0] ALU_OUTPUT
);

  wire alu_1_eq;
  wire [1:0] ctl3_1_funcalu, ctl4_1_muxpc;
  wire [15:0] adder_1_out, multiplexer_1_out;

  Adder #(.width(16)) adder_1 (.a(PC), .b(16'h1), .out(adder_1_out));  // open: cin, cout
  CTL4 ctl4_1 (.OP(OP), .MUXpc(ctl4_1_muxpc));
  CTL3 ctl3_1 (.OP(OP), .MUXpc(MUXpc), .FUNCalu(ctl3_1_funcalu), .EQ(alu_1_eq));
  Adder #(.width(16)) adder_2 (.a(OPERAND0), .b(adder_1_out), .out(MUXpc_v1));  // open: cin, cout
  Multiplexer #(.select(2), .width(16), .disabled(0), .enable("false")) multiplexer_1 (
    .in1(OPERAND0), .in2(OPERAND2), .in3(adder_1_out), .out(multiplexer_1_out), .sel(ctl4_1_muxpc));  // open: in0
  ALU alu_1 (
    .ALUfunc(ctl3_1_funcalu), .EQ(alu_1_eq), .SRC2(multiplexer_1_out), .SRC1(OPERAND1),
    .ALU_OUTPUT(ALU_OUTPUT));

  assign MUXpc_v2 = OPERAND1;
  assign OP_2 = OP;
  assign PC_2 = PC;
  assign rT_2 = rT;
  assign STORE_DATA = OPERAND2;
endmodule

module CTL3 (
  input  [2:0] OP,
  input  EQ,
  output [1:0] MUXpc,
  output [1:0] FUNCalu
);

  wire comparator_2_eq, comparator_4_eq, comparator_5_eq;
  wire [0:0] comparator_3_eq;
  wire [1:1] or_1_out;

  Comparator #(.width(3)) comparator_1 (.a(3'b111), .b(OP), .eq(MUXpc[1]));  // open: gt, lt
  Comparator #(.width(3)) comparator_2 (.a(3'b110), .b(OP), .eq(comparator_2_eq));  // open: gt, lt
  Comparator #(.width(3)) comparator_3 (.a(3'b010), .b(OP), .eq(comparator_3_eq[0]));  // open: gt, lt
  Comparator #(.width(3)) comparator_4 (.a(3'b011), .b(OP), .eq(comparator_4_eq));  // open: gt, lt
  Comparator #(.width(3)) comparator_5 (.a(3'b111), .b(OP), .eq(comparator_5_eq));  // open: gt, lt
  and and_1 (MUXpc[0], comparator_2_eq, EQ);
  or or_1 (or_1_out[1], comparator_4_eq, comparator_5_eq);
  assign FUNCalu = {1'b0, comparator_3_eq[0]} | {or_1_out[1], 1'b0};  // OR_Gate or_2, 2 bits wide

  // Notes on the sheet:
  //   JALR
  //   BEQ
endmodule

module ALU (
  input  [15:0] SRC2,
  input  [15:0] SRC1,
  input  [1:0] ALUfunc,
  output EQ,
  output [15:0] ALU_OUTPUT
);

  wire [15:0] adder_1_out, nand_1_out;

  assign nand_1_out = ~(SRC2 & SRC1);  // NAND_Gate nand_1, 16 bits wide
  Multiplexer #(.select(2), .width(16), .disabled(0), .enable("false")) multiplexer_1 (
    .in0(adder_1_out), .in1(nand_1_out), .in2(SRC2), .out(ALU_OUTPUT), .sel(ALUfunc));  // open: in3
  Adder #(.width(16)) adder_1 (.a(SRC2), .b(SRC1), .out(adder_1_out));  // open: cin, cout
  Comparator #(.width(16)) comparator_1 (.a(SRC1), .b(SRC2), .eq(EQ));  // open: gt, lt
endmodule

module CTL4 (
  input  [2:0] OP,
  output [1:0] MUXpc
);

  wire and_2_out, and_3_out, not_1_out, not_2_out, not_3_out, not_4_out;
  wire [0:0] or_1_out;
  wire [1:1] and_1_out, and_4_out;

  and and_1 (and_1_out[1], OP[0], OP[1], OP[2]);
  not not_1 (not_1_out, and_1_out[1]);
  not not_2 (not_2_out, OP[0]);
  not not_3 (not_3_out, OP[1]);
  and and_2 (and_2_out, not_1_out, OP[0]);
  and and_3 (and_3_out, not_2_out, not_3_out, OP[2]);
  not not_4 (not_4_out, or_1_out[0]);
  and and_4 (and_4_out[1], not_4_out, not_1_out);
  or or_1 (or_1_out[0], and_2_out, and_3_out);
  assign MUXpc = {2{and_1_out[1]}} | {1'b0, or_1_out[0]} | {and_4_out[1], 1'b0};  // OR_Gate or_2, 2 bits wide

  // Notes on the sheet:
  //   JALR
  //   ADD, NAND, BEQ
  //   ADDI, LUI, LW, SW
endmodule

module MEM (
  input  [2:0] OP,
  input  [2:0] rT,
  input  [15:0] PC,
  input  [15:0] STORE_DATA,
  input  [15:0] ALU_OUTPUT,
  output [2:0] rT_2,
  output [15:0] RF_WRITE_DATA
);

  wire clock_1_out, ctl2_1_muxout, ctl2_1_wedmem, not_1_out;
  wire [15:0] ram_1_data;

  CTL2 ctl2_1 (.OP(OP), .WEdmem(ctl2_1_wedmem), .MUXout(ctl2_1_muxout));
  not not_1 (not_1_out, clock_1_out);
  Clock clock_1 (.out(clock_1_out));
  RAM #(.addrWidth(16), .dataWidth(16), .bus("separate")) ram_1 (
    .addr(ALU_OUTPUT), .din(STORE_DATA), .data(ram_1_data), .str(ctl2_1_wedmem), .sel(1'b1), .clk(not_1_out),
    .ld(1'b1));  // open: clr
  Multiplexer #(.width(16), .disabled(0), .enable("false")) multiplexer_1 (
    .in0(ALU_OUTPUT), .in1(ram_1_data), .out(RF_WRITE_DATA), .sel(ctl2_1_muxout));

  assign rT_2 = rT;
endmodule

module CTL2 (
  input  [2:0] OP,
  output WEdmem,
  output MUXout
);

  Comparator #(.width(3)) comparator_1 (.a(OP), .b(3'b101), .eq(WEdmem));  // open: gt, lt
  Comparator #(.width(3)) comparator_2 (.a(OP), .b(3'b100), .eq(MUXout));  // open: gt, lt
endmodule

module WB (
  input  [2:0] rT,
  input  [15:0] RF_WRITE_DATA,
  input  [2:0] rT_2,
  output WErf,
  output [15:0] TGT_value,
  output [2:0] TGT_adress,
  output [15:0] RF_WRITE_DATA_2
);

  CTL1 ctl1_1 (.rT(rT), .WErf(WErf));

  assign RF_WRITE_DATA_2 = RF_WRITE_DATA;
  assign rT_2 = rT;
  assign TGT_adress = rT;
  assign TGT_value = RF_WRITE_DATA;
endmodule

module CTL1 (
  input  [2:0] rT,
  output WErf
);

  or or_1 (WErf, rT[0], rT[1], rT[2]);
endmodule

module MAIN (
  output [2:0] out_1
);

  wire clock_1_out, clock_2_out, clock_3_out, clock_4_out, clock_5_out, clock_6_out, wb_1_werf;
  wire [1:0] ex_1_muxpc;
  wire [2:0] ex_1_op_2, ex_1_rt_2, id_1_op_2, id_1_rt, if_1_op, if_1_ra, if_1_rb, if_1_rc, mem_1_rt_2,
       register_3_q, register_5_q, register_6_q, register_7_q, register_12_q, register_13_q, register_17_q,
       register_18_q, register_20_q, undriven, wb_1_tgt_adress;
  wire [3:0] if_1_out_6, register_4_q;
  wire [15:0] ex_1_alu_output, ex_1_muxpc_v1, ex_1_muxpc_v2, ex_1_pc_2, ex_1_store_data, id_1_operand0,
       id_1_operand1, id_1_operand2, id_1_pc_2, if_1_pc_1, if_1_pc_2, mem_1_rf_write_data, multiplexer_1_out,
       register_1_q, register_2_q, register_8_q, register_9_q, register_10_q, register_11_q, register_14_q,
       register_15_q, register_16_q, register_19_q, wb_1_rf_write_data_2, wb_1_tgt_value;

  Multiplexer #(.select(2), .width(16), .disabled(0), .enable("false")) multiplexer_1 (
    .in0(if_1_pc_1), .in1(ex_1_muxpc_v1), .in2(ex_1_muxpc_v2), .out(multiplexer_1_out), .sel(ex_1_muxpc));  // open: in3
  Clock clock_1 (.out(clock_1_out));
  IF if_1 (
    .PC(register_1_q), .OP(if_1_op), .rA(if_1_ra), .rB(if_1_rb), .out_6(if_1_out_6), .rC(if_1_rc),
    .PC_2(if_1_pc_2), .PC_1(if_1_pc_1));
  Register #(.width(16)) register_1 (
    .D(multiplexer_1_out), .en(1'b1), .Q(register_1_q), .clk(clock_1_out));  // open: clr
  Register #(.width(16)) register_2 (.D(if_1_pc_2), .en(1'b1), .Q(register_2_q), .clk(clock_2_out));  // open: clr
  Register #(.width(3)) register_3 (.D(if_1_rc), .en(1'b1), .Q(register_3_q), .clk(clock_2_out));  // open: clr
  Register #(.width(4)) register_4 (.D(if_1_out_6), .en(1'b1), .Q(register_4_q), .clk(clock_2_out));  // open: clr
  Register #(.width(3)) register_5 (.D(if_1_rb), .en(1'b1), .Q(register_5_q), .clk(clock_2_out));  // open: clr
  Register #(.width(3)) register_6 (.D(if_1_ra), .en(1'b1), .Q(register_6_q), .clk(clock_2_out));  // open: clr
  Register #(.width(3)) register_7 (.D(if_1_op), .en(1'b1), .Q(register_7_q), .clk(clock_2_out));  // open: clr
  Clock clock_2 (.out(clock_2_out));
  ID id_1 (
    .TGT_Value(wb_1_tgt_value), .TGT_Adress(wb_1_tgt_adress), .WErf(wb_1_werf), .OP(register_7_q),
    .rA(register_6_q), .rB(register_5_q), .in_4(register_4_q), .rC(register_3_q), .PC(register_2_q),
    .OP_2(id_1_op_2), .rT(id_1_rt), .PC_2(id_1_pc_2), .OPERAND0(id_1_operand0), .OPERAND2(id_1_operand2),
    .OPERAND1(id_1_operand1));
  Register #(.width(16)) register_8 (.D(id_1_operand1), .en(1'b1), .Q(register_8_q), .clk(clock_3_out));  // open: clr
  Register #(.width(16)) register_9 (.D(id_1_operand2), .en(1'b1), .Q(register_9_q), .clk(clock_3_out));  // open: clr
  Register #(.width(16)) register_10 (.D(id_1_operand0), .en(1'b1), .Q(register_10_q), .clk(clock_3_out));  // open: clr
  Register #(.width(16)) register_11 (.D(id_1_pc_2), .en(1'b1), .Q(register_11_q), .clk(clock_3_out));  // open: clr
  Register #(.width(3)) register_12 (.D(id_1_rt), .en(1'b1), .Q(register_12_q), .clk(clock_3_out));  // open: clr
  Register #(.width(3)) register_13 (.D(id_1_op_2), .en(1'b1), .Q(register_13_q), .clk(clock_3_out));  // open: clr
  Clock clock_3 (.out(clock_3_out));
  EX ex_1 (
    .OP(register_13_q), .rT(register_12_q), .PC(register_11_q), .OPERAND0(register_10_q),
    .OPERAND2(register_9_q), .OPERAND1(register_8_q), .OP_2(ex_1_op_2), .rT_2(ex_1_rt_2), .PC_2(ex_1_pc_2),
    .STORE_DATA(ex_1_store_data), .ALU_OUTPUT(ex_1_alu_output), .MUXpc(ex_1_muxpc), .MUXpc_v1(ex_1_muxpc_v1),
    .MUXpc_v2(ex_1_muxpc_v2));
  Register #(.width(16)) register_14 (
    .D(ex_1_alu_output), .en(1'b1), .Q(register_14_q), .clk(clock_4_out));  // open: clr
  Register #(.width(16)) register_15 (
    .D(ex_1_store_data), .en(1'b1), .Q(register_15_q), .clk(clock_4_out));  // open: clr
  Register #(.width(16)) register_16 (.D(ex_1_pc_2), .en(1'b1), .Q(register_16_q), .clk(clock_4_out));  // open: clr
  Register #(.width(3)) register_17 (.D(ex_1_rt_2), .en(1'b1), .Q(register_17_q), .clk(clock_4_out));  // open: clr
  Register #(.width(3)) register_18 (.D(ex_1_op_2), .en(1'b1), .Q(register_18_q), .clk(clock_4_out));  // open: clr
  MEM mem_1 (
    .OP(register_18_q), .rT(register_17_q), .PC(register_16_q), .STORE_DATA(register_15_q),
    .ALU_OUTPUT(register_14_q), .rT_2(mem_1_rt_2), .RF_WRITE_DATA(mem_1_rf_write_data));
  Clock clock_4 (.out(clock_4_out));
  Register #(.width(16)) register_19 (
    .D(mem_1_rf_write_data), .en(1'b1), .Q(register_19_q), .clk(clock_5_out));  // open: clr
  Register #(.width(3)) register_20 (.D(mem_1_rt_2), .en(1'b1), .Q(register_20_q), .clk(clock_5_out));  // open: clr
  Clock clock_5 (.out(clock_5_out));
  WB wb_1 (
    .rT(register_20_q), .RF_WRITE_DATA(register_19_q), .rT_2(undriven),
    .RF_WRITE_DATA_2(wb_1_rf_write_data_2), .WErf(wb_1_werf), .TGT_value(wb_1_tgt_value),
    .TGT_adress(wb_1_tgt_adress));
  Register #(.width(16)) register_21 (.D(wb_1_rf_write_data_2), .en(1'b1), .clk(clock_6_out));  // open: Q, clr
  Register #(.width(3)) register_22 (.D(undriven), .en(1'b1), .Q(out_1), .clk(clock_6_out));  // open: clr
  Clock clock_6 (.out(clock_6_out));
endmodule
