// Logisim project risk16.circ as structural Verilog: 20 circuits, main circuit IF
module IF (
  input  [15:0] PC,
  output [15:0] PC_1,
  output [2:0] OP,
  output [2:0] rA,
  output [2:0] rB,
  output [3:0] out_6,
  output [2:0] rC,
  output [15:0] PC_2
);

  ROM #(.addrWidth(16), .dataWidth(16)) rom_1 (.addr(PC), .data({OP, rA, rB, out_6, rC}), .sel(1'b1));
  Adder #(.width(16)) adder_1 (.a(PC), .b(16'h1), .out(PC_1));  // open: cin, cout

  assign PC_2 = PC;

  // Notes on the sheet:
  //   contents of rom_1 (hex, n*v repeats v):
  //   6403 2488 a407 2400 8807 a500 8407 2481 a407 6420 24a0 8807 a500 8407 2481 a407 6411 2480 8807 a500
  //   8407 2481 a407 643f 24a0 8807 a500 8407 2481 a407 646e 24b0 8807 a500 8407 2481 a407 64ff 24b8 8807
  //   a500 8407 2481 a407 64bf 24a8 8807 a500 8407 2481 a407 64a0 24a8 8807 a500 8407 2481 a407 641b 2480
  //   8807 a500 8407 2481 a407 2400 8807 a500 8407 2481 a407 2400 8807 a500 8407 2481 a407 2400 8807 a500
  //   8407 2481 a407 2400 8807 a500 8407 2481 a407 2400 8807 a500 8407 2481 a407 2400 8807 a500 8407 2481
  //   a407 2400 8807 a500 8407 2481 a407 2400 a402 6403 2488 a407 6401 24a4 a408 2401 a405 0 8402 2810
  //   c518 8402 9007 9200 6bff 2930 901 b100 8407 2481 a407 8405 8808 a500 8405 8805 482 a405 8408 2481
  //   a408 8402 2481 a402 c064 0 2408 a406 6401 2487 6bff 292f a500 6401 24af 6bff 292f a500 2420 6bff
  //   292f a500 2421 6bff 292f a500 0 2401 c42f 6401 24a4 8806 482 a408 8408 8480 6bff 2930 a50f 6bff 2920
  //   8500 a401 8401 6801 2921 c501 c00a 0 8406 2800 c504 8406 24ff a406 c001 0 0 0 8401 6801 2922 c501
  //   c00a 0 8406 280f c504 8406 2481 a406 c001 0 0 0 c001 c030 0 c001 c04a 0 8401 2820 c501 c015 0 240f
  //   a403 8408 8480 a404 0 8403 2800 c53a 8403 24ff a403 6403 2488 8803 482 a407 8407 8480 c001 c02f 0
  //   4481 8804 4902 4482 a400 8403 9000 6bff 2930 901 b100 8407 8480 8804 4482 4481 c001 c01e 0 c001 c04e
  //   0 c40c 8407 8480 8804 4c82 4483 4903 4482 8807 a500 2400 a404 c001 0 0 8403 9007 9200 6bff 2930 901
  //   b100 c042 0 0 c064
endmodule

module ID (
  input  [2:0] OP,
  input  [2:0] rA,
  input  [2:0] rB,
  input  [3:0] in_4,
  input  [2:0] rC,
  input  [15:0] PC,
  input  [2:0] OP_EXE,
  input  [2:0] rT_EXE,
  input  [15:0] TGT_Value,
  input  [2:0] TGT_Adress,
  input  WErf,
  output STALL,
  output [2:0] OP_2,
  output [2:0] rT,
  output [2:0] s1,
  output [2:0] s2,
  output [15:0] PC_2,
  output [15:0] OPERAND0,
  output [15:0] OPERAND2,
  output [15:0] OPERAND1
);

  wire ctl6_1_muxop0, ctl6_1_muxs2;

  CTL7 ctl7_1 (
    .OP_EXE(OP_EXE), .rT_EXE(rT_EXE), .OP(OP), .rA(rA), .rB(rB), .rC(rC), .OP_2(OP_2), .rT(rT), .STALL(STALL));
  CTL6 ctl6_1 (.OP(OP_2), .MUXs2(ctl6_1_muxs2), .MUXop0(ctl6_1_muxop0));
  Multiplexer #(.width(3), .disabled(0), .enable("false")) multiplexer_1 (
    .in0(rA), .in1(rC), .out(s2), .sel(ctl6_1_muxs2));
  Multiplexer #(.width(16), .disabled(0), .enable("false")) multiplexer_2 (
    .in0({{10{in_4[3]}}, in_4[2:0], rC}), .in1({rB, in_4, rC, {6{1'b0}}}), .out(OPERAND0), .sel(ctl6_1_muxop0));
  REGISTER_FILE register_file_1 (
    .TGT_2(TGT_Adress), .SRC1(rB), .SRC2(s2), .TGT(TGT_Value), .WErf(WErf), .SRC2_2(OPERAND2),
    .SRC1_2(OPERAND1));

  assign PC_2 = PC;
  assign s1 = rB;

  // Notes on the sheet:
  //   Sign-Ext-7
  //   Left-Shift-6
endmodule

module REGISTER_FILE (
  input  [15:0] TGT,
  input  [2:0] TGT_2,
  input  [2:0] SRC1,
  input  [2:0] SRC2,
  input  WErf,
  output [15:0] SRC2_2,
  output [15:0] SRC1_2
);

  wire clock_1_out, demultiplexer_1_out1, demultiplexer_1_out2, demultiplexer_1_out3, demultiplexer_1_out4,
       demultiplexer_1_out5, demultiplexer_1_out6, demultiplexer_1_out7;
  wire [15:0] multiplexer_1_out, multiplexer_2_out, multiplexer_3_out, multiplexer_4_out, multiplexer_5_out,
       multiplexer_6_out, multiplexer_7_out, register_1_q, register_2_q, register_3_q, register_4_q,
       register_5_q, register_6_q, register_7_q;

  Demultiplexer #(.select(3), .disabled(0), .enable("false")) demultiplexer_1 (
    .out1(demultiplexer_1_out1), .out2(demultiplexer_1_out2), .out3(demultiplexer_1_out3),
    .out4(demultiplexer_1_out4), .out5(demultiplexer_1_out5), .out6(demultiplexer_1_out6),
    .out7(demultiplexer_1_out7), .in(WErf), .sel(TGT_2));  // open: out0
  Multiplexer #(.width(16), .disabled(0), .enable("false")) multiplexer_1 (
    .in0(register_1_q), .in1(TGT), .out(multiplexer_1_out), .sel(demultiplexer_1_out1));
  Register #(.width(16), .trigger("falling")) register_1 (
    .D(multiplexer_1_out), .en(1'b1), .Q(register_1_q), .clk(clock_1_out));  // open: clr
  Register #(.width(16), .trigger("falling")) register_2 (
    .D(multiplexer_2_out), .en(1'b1), .Q(register_2_q), .clk(clock_1_out));  // open: clr
  Multiplexer #(.width(16), .disabled(0), .enable("false")) multiplexer_2 (
    .in0(register_2_q), .in1(TGT), .out(multiplexer_2_out), .sel(demultiplexer_1_out2));
  Multiplexer #(.width(16), .disabled(0), .enable("false")) multiplexer_3 (
    .in0(register_3_q), .in1(TGT), .out(multiplexer_3_out), .sel(demultiplexer_1_out3));
  Register #(.width(16), .trigger("falling")) register_3 (
    .D(multiplexer_3_out), .en(1'b1), .Q(register_3_q), .clk(clock_1_out));  // open: clr
  Multiplexer #(.width(16), .disabled(0), .enable("false")) multiplexer_4 (
    .in0(register_4_q), .in1(TGT), .out(multiplexer_4_out), .sel(demultiplexer_1_out4));
  Register #(.width(16), .trigger("falling")) register_4 (
    .D(multiplexer_4_out), .en(1'b1), .Q(register_4_q), .clk(clock_1_out));  // open: clr
  Multiplexer #(.width(16), .disabled(0), .enable("false")) multiplexer_5 (
    .in0(register_5_q), .in1(TGT), .out(multiplexer_5_out), .sel(demultiplexer_1_out5));
  Register #(.width(16), .trigger("falling")) register_5 (
    .D(multiplexer_5_out), .en(1'b1), .Q(register_5_q), .clk(clock_1_out));  // open: clr
  Multiplexer #(.width(16), .disabled(0), .enable("false")) multiplexer_6 (
    .in0(register_6_q), .in1(TGT), .out(multiplexer_6_out), .sel(demultiplexer_1_out6));
  Register #(.width(16), .trigger("falling")) register_6 (
    .D(multiplexer_6_out), .en(1'b1), .Q(register_6_q), .clk(clock_1_out));  // open: clr
  Multiplexer #(.width(16), .disabled(0), .enable("false")) multiplexer_7 (
    .in0(register_7_q), .in1(TGT), .out(multiplexer_7_out), .sel(demultiplexer_1_out7));
  Register #(.width(16), .trigger("falling")) register_7 (
    .D(multiplexer_7_out), .en(1'b1), .Q(register_7_q), .clk(clock_1_out));  // open: clr
  Clock clock_1 (.out(clock_1_out));
  Multiplexer #(.select(3), .width(16), .disabled(0), .enable("false")) multiplexer_8 (
    .in0({16{1'b0}}), .in1(register_1_q), .in2(register_2_q), .in3(register_3_q), .in4(register_4_q),
    .in5(register_5_q), .in6(register_6_q), .in7(register_7_q), .out(SRC1_2), .sel(SRC1));
  Multiplexer #(.select(3), .width(16), .enable("false")) multiplexer_9 (
    .in0({16{1'b0}}), .in1(register_1_q), .in2(register_2_q), .in3(register_3_q), .in4(register_4_q),
    .in5(register_5_q), .in6(register_6_q), .in7(register_7_q), .out(SRC2_2), .sel(SRC2));
endmodule

module CTL7 (
  input  [2:0] OP,
  input  [2:0] rA,
  input  [2:0] rB,
  input  [2:0] rC,
  input  [2:0] OP_EXE,
  input  [2:0] rT_EXE,
  output [2:0] OP_2,
  output [2:0] rT,
  output STALL
);

  wire and_1_out, and_2_out, and_3_out, and_4_out, and_5_out, and_6_out, comparator_1_eq, comparator_2_eq,
       comparator_3_eq, comparator_4_eq, or_1_out, or_2_out, xor_1_out, xor_2_out;

  Comparator #(.width(3)) comparator_1 (.a(3'b100), .b(OP_EXE), .eq(comparator_1_eq));  // open: gt, lt
  xor xor_1 (xor_1_out, OP[0], OP[1]);
  and and_1 (and_1_out, xor_1_out, OP[2]);
  Multiplexer #(.width(3), .disabled(0), .enable("false")) multiplexer_1 (
    .in0(rA), .in1(3'b000), .out(rT), .sel(and_1_out));
  xor xor_2 (xor_2_out, OP[0], OP[1]);
  Comparator #(.width(3)) comparator_2 (.a(rA), .b(rT_EXE), .eq(comparator_2_eq));  // open: gt, lt
  or or_1 (or_1_out, ~OP[0], ~OP[1], OP[2]);  // OR_Gate
  Comparator #(.width(3)) comparator_3 (.a(rB), .b(rT_EXE), .eq(comparator_3_eq));  // open: gt, lt
  and and_2 (and_2_out, ~OP[0], ~OP[2]);  // AND_Gate
  Comparator #(.width(3)) comparator_4 (.a(rC), .b(rT_EXE), .eq(comparator_4_eq));  // open: gt, lt
  and and_3 (and_3_out, xor_2_out, OP[2]);
  and and_4 (and_4_out, and_3_out, comparator_2_eq);
  and and_5 (and_5_out, or_1_out, comparator_3_eq);
  and and_6 (and_6_out, and_2_out, comparator_4_eq);
  or or_2 (or_2_out, and_4_out, and_5_out, and_6_out);
  and and_7 (STALL, comparator_1_eq, or_2_out);

  assign OP_2 = OP;
endmodule

module CTL6 (
  input  [2:0] OP,
  output MUXs2,
  output MUXop0
);

  wire not_1_out, not_2_out, not_3_out;

  and and_1 (MUXs2, not_2_out, not_1_out);
  not not_1 (not_1_out, OP[0]);
  not not_2 (not_2_out, OP[2]);
  not not_3 (not_3_out, OP[2]);
  and and_2 (MUXop0, not_3_out, OP[1], OP[0]);
endmodule

module EX (
  input  [2:0] OP,
  input  [2:0] rT,
  input  [2:0] s1,
  input  [2:0] s2,
  input  [15:0] PC,
  input  [15:0] OPERAND0,
  input  [15:0] OPERAND2,
  input  [15:0] OPERAND1,
  input  [15:0] MEM_value,
  input  [15:0] WB_value,
  input  [15:0] END_value,
  input  [2:0] MEM_adress,
  input  [2:0] WB_adress,
  input  [2:0] END_adress,
  output [1:0] MUXpc,
  output STOMP,
  output [15:0] MUXpc_v1,
  output [15:0] MUXpc_v2,
  output [2:0] OP_2,
  output [2:0] rT_2,
  output [15:0] PC_2,
  output [15:0] STORE_DATA,
  output [15:0] ALU_OUTPUT
);

  wire alu_1_eq;
  wire [1:0] ctl3_1_funcalu, ctl4_1_muxpc, ctl5_1_muxalu2, ctl5_1_muxalu2_2;
  wire [15:0] adder_1_out, multiplexer_3_out;

  CTL5 ctl5_1 (
    .MEM_adress(MEM_adress), .WB_adress(WB_adress), .END_adress(END_adress), .s1(s1), .s2(s2),
    .MUXalu2(ctl5_1_muxalu2), .MUXalu2_2(ctl5_1_muxalu2_2));
  Adder #(.width(16)) adder_1 (.a(PC), .b(16'h1), .out(adder_1_out));  // open: cin, cout
  CTL4 ctl4_1 (.OP(OP), .MUXpc(ctl4_1_muxpc));
  CTL3 ctl3_1 (.OP(OP), .MUXpc(MUXpc), .STOMP(STOMP), .FUNCalu(ctl3_1_funcalu), .EQ(alu_1_eq));
  Adder #(.width(16)) adder_2 (.a(OPERAND0), .b(adder_1_out), .out(MUXpc_v1));  // open: cin, cout
  Multiplexer #(.select(2), .width(16), .disabled(0), .enable("false")) multiplexer_1 (
    .in0(OPERAND2), .in1(MEM_value), .in2(WB_value), .in3(END_value), .out(STORE_DATA), .sel(ctl5_1_muxalu2_2));
  Multiplexer #(.select(2), .width(16), .disabled(0), .enable("false")) multiplexer_2 (
    .in0(OPERAND1), .in1(MEM_value), .in2(WB_value), .in3(END_value), .out(MUXpc_v2), .sel(ctl5_1_muxalu2));
  Multiplexer #(.select(2), .width(16), .disabled(0), .enable("false")) multiplexer_3 (
    .in1(OPERAND0), .in2(STORE_DATA), .in3(adder_1_out), .out(multiplexer_3_out), .sel(ctl4_1_muxpc));  // open: in0
  ALU alu_1 (
    .ALUfunc(ctl3_1_funcalu), .EQ(alu_1_eq), .SRC2(multiplexer_3_out), .SRC1(MUXpc_v2),
    .ALU_OUTPUT(ALU_OUTPUT));

  assign OP_2 = OP;
  assign PC_2 = PC;
  assign rT_2 = rT;
endmodule

module CTL3 (
  input  [2:0] OP,
  input  EQ,
  output [1:0] MUXpc,
  output STOMP,
  output [1:0] FUNCalu
);

  wire comparator_2_eq, comparator_4_eq, comparator_5_eq;
  wire [0:0] comparator_3_eq;
  wire [1:1] or_2_out;

  Comparator #(.width(3)) comparator_1 (.a(3'b111), .b(OP), .eq(MUXpc[1]));  // open: gt, lt
  Comparator #(.width(3)) comparator_2 (.a(3'b110), .b(OP), .eq(comparator_2_eq));  // open: gt, lt
  Comparator #(.width(3)) comparator_3 (.a(3'b010), .b(OP), .eq(comparator_3_eq[0]));  // open: gt, lt
  Comparator #(.width(3)) comparator_4 (.a(3'b011), .b(OP), .eq(comparator_4_eq));  // open: gt, lt
  Comparator #(.width(3)) comparator_5 (.a(3'b111), .b(OP), .eq(comparator_5_eq));  // open: gt, lt
  or or_1 (STOMP, MUXpc[0], MUXpc[1]);
  and and_1 (MUXpc[0], comparator_2_eq, EQ);
  or or_2 (or_2_out[1], comparator_4_eq, comparator_5_eq);
  assign FUNCalu = {1'b0, comparator_3_eq[0]} | {or_2_out[1], 1'b0};  // OR_Gate or_3, 2 bits wide

  // Notes on the sheet:
  //   JALR
  //   BEQ
endmodule

module ALU (
  input  [15:0] SRC2,
  input  [15:0] SRC1,
  input  [1:0] ALUfunc,
  output EQ,
  output [15:0] ALU_OUTPUT
);

  wire [15:0] adder_1_out, nand_1_out;

  assign nand_1_out = ~(SRC2 & SRC1);  // NAND_Gate nand_1, 16 bits wide
  Multiplexer #(.select(2), .width(16), .disabled(0), .enable("false")) multiplexer_1 (
    .in0(adder_1_out), .in1(nand_1_out), .in2(SRC2), .out(ALU_OUTPUT), .sel(ALUfunc));  // open: in3
  Adder #(.width(16)) adder_1 (.a(SRC2), .b(SRC1), .out(adder_1_out));  // open: cin, cout
  Comparator #(.width(16)) comparator_1 (.a(SRC1), .b(SRC2), .eq(EQ));  // open: gt, lt
endmodule

module CTL4 (
  input  [2:0] OP,
  output [1:0] MUXpc
);

  wire and_2_out, and_3_out, not_1_out, not_2_out, not_3_out, not_4_out;
  wire [0:0] or_1_out;
  wire [1:1] and_1_out, and_4_out;

  and and_1 (and_1_out[1], OP[0], OP[1], OP[2]);
  not not_1 (not_1_out, and_1_out[1]);
  not not_2 (not_2_out, OP[0]);
  not not_3 (not_3_out, OP[1]);
  and and_2 (and_2_out, not_1_out, OP[0]);
  and and_3 (and_3_out, not_2_out, not_3_out, OP[2]);
  not not_4 (not_4_out, or_1_out[0]);
  and and_4 (and_4_out[1], not_4_out, not_1_out);
  or or_1 (or_1_out[0], and_2_out, and_3_out);
  assign MUXpc = {2{and_1_out[1]}} | {1'b0, or_1_out[0]} | {and_4_out[1], 1'b0};  // OR_Gate or_2, 2 bits wide

  // Notes on the sheet:
  //   JALR
  //   ADD, NAND, BEQ
  //   ADDI, LUI, LW, SW
endmodule

module MEM (
  input  [2:0] OP,
  input  [2:0] rT,
  input  [15:0] PC,
  input  [15:0] STORE_DATA,
  input  [15:0] ALU_OUTPUT,
  input  [15:0] RAM_DATA_OUT,
  output [2:0] Bypass_adress,
  output [15:0] Bypass_value,
  output [15:0] RAM_DATA_IN,
  output [15:0] RAM_ADDR,
  output RAM_WE,
  output RAM_RE,
  output [2:0] rT_2,
  output [15:0] RF_WRITE_DATA
);

  wire ctl2_1_muxout;

  CTL2 ctl2_1 (.OP(OP), .WEdmem(RAM_WE), .REdmem(RAM_RE), .MUXout(ctl2_1_muxout));
  Multiplexer #(.width(16), .disabled(0), .enable("false")) multiplexer_1 (
    .in0(ALU_OUTPUT), .in1(RAM_DATA_OUT), .out(RF_WRITE_DATA), .sel(ctl2_1_muxout));

  assign Bypass_adress = rT;
  assign Bypass_value = ALU_OUTPUT;
  assign RAM_ADDR = ALU_OUTPUT;
  assign RAM_DATA_IN = STORE_DATA;
  assign rT_2 = rT;
endmodule

module CTL2 (
  input  [2:0] OP,
  output WEdmem,
  output REdmem,
  output MUXout
);

  Comparator #(.width(3)) comparator_1 (.a(OP), .b(3'b101), .eq(WEdmem));  // open: gt, lt
  Comparator #(.width(3)) comparator_2 (.a(OP), .b(3'b100), .eq(REdmem));  // open: gt, lt
  Comparator #(.width(3)) comparator_3 (.a(OP), .b(3'b100), .eq(MUXout));  // open: gt, lt
endmodule

module WB (
  input  [2:0] rT,
  input  [15:0] RF_WRITE_DATA,
  input  [2:0] rT_2,
  output WErf,
  output [15:0] TGT_value,
  output [2:0] TGT_adress,
  output [15:0] RF_WRITE_DATA_2
);

  CTL1 ctl1_1 (.rT(rT), .WErf(WErf));

  assign RF_WRITE_DATA_2 = RF_WRITE_DATA;
  assign rT_2 = rT;
  assign TGT_adress = rT;
  assign TGT_value = RF_WRITE_DATA;
endmodule

module CTL1 (
  input  [2:0] rT,
  output WErf
);

  or or_1 (WErf, rT[0], rT[1], rT[2]);
endmodule

module PIPELINE (
  input  [6:0] KEYBOARD_VALUE,
  output [3:0] SCREEN_ADRESS,
  output [15:0] SCREEN_VALUE,
  output SCREEN_ENABLE,
  output [6:0] TTY_VALUE,
  output TTY_ENABLE,
  output KEYBOARD_ENABLE
);

  wire clock_1_out, clock_2_out, clock_3_out, clock_4_out, clock_5_out, clock_6_out, mem_1_ram_re,
       mem_1_ram_we, or_1_out, wb_1_werf;
  wire [1:0] ex_1_muxpc, ex_1_stomp;
  wire [2:0] ex_1_op_2, ex_1_rt_2, id_1_op_2, id_1_rt, id_1_s1, id_1_s2, if_1_op, if_1_ra, if_1_rb, if_1_rc,
       mem_1_bypass_adress, mem_1_rt_2, multiplexer_4_out, multiplexer_6_out, multiplexer_7_out,
       multiplexer_8_out, multiplexer_13_out, multiplexer_14_out, multiplexer_15_out, multiplexer_16_out,
       register_3_q, register_5_q, register_6_q, register_7_q, register_12_q, register_13_q, register_14_q,
       register_15_q, register_19_q, register_20_q, register_22_q, register_24_q, undriven, wb_1_tgt_adress;
  wire [3:0] if_1_out_6, multiplexer_5_out, register_4_q;
  wire [15:0] ex_1_alu_output, ex_1_muxpc_v1, ex_1_muxpc_v2, ex_1_pc_2, ex_1_store_data, id_1_operand0,
       id_1_operand1, id_1_operand2, id_1_pc_2, if_1_pc_1, if_1_pc_2, mem_1_bypass_value, mem_1_ram_addr,
       mem_1_ram_data_in, mem_1_rf_write_data, memory_mapping_1_data_out, multiplexer_1_out,
       multiplexer_2_out, multiplexer_3_out, multiplexer_9_out, multiplexer_10_out, multiplexer_11_out,
       multiplexer_12_out, register_1_q, register_2_q, register_8_q, register_9_q, register_10_q,
       register_11_q, register_16_q, register_17_q, register_18_q, register_21_q, register_23_q,
       wb_1_rf_write_data_2, wb_1_tgt_value;

  Multiplexer #(.select(2), .width(16), .disabled(0), .enable("false")) multiplexer_1 (
    .in0(if_1_pc_1), .in1(ex_1_muxpc_v1), .in2(ex_1_muxpc_v2), .out(multiplexer_1_out), .sel(ex_1_muxpc));  // open: in3
  Register #(.width(16)) register_1 (
    .D(multiplexer_2_out), .en(1'b1), .Q(register_1_q), .clk(clock_1_out));  // open: clr
  Multiplexer #(.width(16), .disabled(0), .enable("false")) multiplexer_2 (
    .in0(multiplexer_1_out), .in1(register_1_q), .out(multiplexer_2_out), .sel(ex_1_stomp[1]));
  Clock clock_1 (.out(clock_1_out));
  IF if_1 (
    .PC(register_1_q), .OP(if_1_op), .rA(if_1_ra), .rB(if_1_rb), .out_6(if_1_out_6), .rC(if_1_rc),
    .PC_2(if_1_pc_2), .PC_1(if_1_pc_1));
  Multiplexer #(.select(2), .width(16), .disabled(0), .enable("false")) multiplexer_3 (
    .in0(if_1_pc_2), .in1({16{1'b0}}), .in2(register_2_q), .out(multiplexer_3_out), .sel(ex_1_stomp));  // open: in3
  Multiplexer #(.select(2), .width(3), .disabled(0), .enable("false")) multiplexer_4 (
    .in0(if_1_rc), .in1(3'b000), .in2(register_3_q), .out(multiplexer_4_out), .sel(ex_1_stomp));  // open: in3
  Multiplexer #(.select(2), .width(4), .disabled(0), .enable("false")) multiplexer_5 (
    .in0(if_1_out_6), .in1(4'b0000), .in2(register_4_q), .out(multiplexer_5_out), .sel(ex_1_stomp));  // open: in3
  Multiplexer #(.select(2), .width(3), .disabled(0), .enable("false")) multiplexer_6 (
    .in0(if_1_rb), .in1(3'b000), .in2(register_5_q), .out(multiplexer_6_out), .sel(ex_1_stomp));  // open: in3
  Multiplexer #(.select(2), .width(3), .disabled(0), .enable("false")) multiplexer_7 (
    .in0(if_1_ra), .in1(3'b000), .in2(register_6_q), .out(multiplexer_7_out), .sel(ex_1_stomp));  // open: in3
  Multiplexer #(.select(2), .width(3), .disabled(0), .enable("false")) multiplexer_8 (
    .in0(if_1_op), .in1(3'b000), .in2(register_7_q), .out(multiplexer_8_out), .sel(ex_1_stomp));  // open: in3
  Register #(.width(16)) register_2 (
    .D(multiplexer_3_out), .en(1'b1), .Q(register_2_q), .clk(clock_2_out));  // open: clr
  Register #(.width(3)) register_3 (
    .D(multiplexer_4_out), .en(1'b1), .Q(register_3_q), .clk(clock_2_out));  // open: clr
  Register #(.width(4)) register_4 (
    .D(multiplexer_5_out), .en(1'b1), .Q(register_4_q), .clk(clock_2_out));  // open: clr
  Register #(.width(3)) register_5 (
    .D(multiplexer_6_out), .en(1'b1), .Q(register_5_q), .clk(clock_2_out));  // open: clr
  Register #(.width(3)) register_6 (
    .D(multiplexer_7_out), .en(1'b1), .Q(register_6_q), .clk(clock_2_out));  // open: clr
  Register #(.width(3)) register_7 (
    .D(multiplexer_8_out), .en(1'b1), .Q(register_7_q), .clk(clock_2_out));  // open: clr
  Clock clock_2 (.out(clock_2_out));
  ID id_1 (
    .OP_EXE(register_15_q), .rT_EXE(register_14_q), .TGT_Value(wb_1_tgt_value), .TGT_Adress(wb_1_tgt_adress),
    .WErf(wb_1_werf), .OP(register_7_q), .rA(register_6_q), .rB(register_5_q), .in_4(register_4_q),
    .rC(register_3_q), .PC(register_2_q), .OP_2(id_1_op_2), .rT(id_1_rt), .s1(id_1_s1), .s2(id_1_s2),
    .PC_2(id_1_pc_2), .OPERAND0(id_1_operand0), .OPERAND2(id_1_operand2), .OPERAND1(id_1_operand1),
    .STALL(ex_1_stomp[1]));
  or or_1 (or_1_out, ex_1_stomp[1], ex_1_stomp[0]);
  Multiplexer #(.width(16), .disabled(0), .enable("false")) multiplexer_9 (
    .in0(id_1_operand1), .in1({16{1'b0}}), .out(multiplexer_9_out), .sel(or_1_out));
  Multiplexer #(.width(16), .disabled(0), .enable("false")) multiplexer_10 (
    .in0(id_1_operand2), .in1({16{1'b0}}), .out(multiplexer_10_out), .sel(or_1_out));
  Multiplexer #(.width(16), .disabled(0), .enable("false")) multiplexer_11 (
    .in0(id_1_operand0), .in1({16{1'b0}}), .out(multiplexer_11_out), .sel(or_1_out));
  Multiplexer #(.width(16), .disabled(0), .enable("false")) multiplexer_12 (
    .in0(id_1_pc_2), .in1({16{1'b0}}), .out(multiplexer_12_out), .sel(or_1_out));
  Multiplexer #(.width(3), .disabled(0), .enable("false")) multiplexer_13 (
    .in0(id_1_s2), .in1(3'b000), .out(multiplexer_13_out), .sel(or_1_out));
  Multiplexer #(.width(3), .disabled(0), .enable("false")) multiplexer_14 (
    .in0(id_1_s1), .in1(3'b000), .out(multiplexer_14_out), .sel(or_1_out));
  Multiplexer #(.width(3), .disabled(0), .enable("false")) multiplexer_15 (
    .in0(id_1_rt), .in1(3'b000), .out(multiplexer_15_out), .sel(or_1_out));
  Multiplexer #(.width(3), .disabled(0), .enable("false")) multiplexer_16 (
    .in0(id_1_op_2), .in1(3'b000), .out(multiplexer_16_out), .sel(or_1_out));
  Register #(.width(16)) register_8 (
    .D(multiplexer_9_out), .en(1'b1), .Q(register_8_q), .clk(clock_3_out));  // open: clr
  Register #(.width(16)) register_9 (
    .D(multiplexer_10_out), .en(1'b1), .Q(register_9_q), .clk(clock_3_out));  // open: clr
  Register #(.width(16)) register_10 (
    .D(multiplexer_11_out), .en(1'b1), .Q(register_10_q), .clk(clock_3_out));  // open: clr
  Register #(.width(16)) register_11 (
    .D(multiplexer_12_out), .en(1'b1), .Q(register_11_q), .clk(clock_3_out));  // open: clr
  Register #(.width(3)) register_12 (
    .D(multiplexer_13_out), .en(1'b1), .Q(register_12_q), .clk(clock_3_out));  // open: clr
  Register #(.width(3)) register_13 (
    .D(multiplexer_14_out), .en(1'b1), .Q(register_13_q), .clk(clock_3_out));  // open: clr
  Register #(.width(3)) register_14 (
    .D(multiplexer_15_out), .en(1'b1), .Q(register_14_q), .clk(clock_3_out));  // open: clr
  Register #(.width(3)) register_15 (
    .D(multiplexer_16_out), .en(1'b1), .Q(register_15_q), .clk(clock_3_out));  // open: clr
  Clock clock_3 (.out(clock_3_out));
  EX ex_1 (
    .MEM_value(mem_1_bypass_value), .WB_value(wb_1_tgt_value), .END_value(register_23_q),
    .MEM_adress(mem_1_bypass_adress), .WB_adress(wb_1_tgt_adress), .END_adress(register_24_q),
    .OP(register_15_q), .rT(register_14_q), .s1(register_13_q), .s2(register_12_q), .PC(register_11_q),
    .OPERAND0(register_10_q), .OPERAND2(register_9_q), .OPERAND1(register_8_q), .OP_2(ex_1_op_2),
    .rT_2(ex_1_rt_2), .PC_2(ex_1_pc_2), .STORE_DATA(ex_1_store_data), .ALU_OUTPUT(ex_1_alu_output),
    .MUXpc(ex_1_muxpc), .STOMP(ex_1_stomp[0]), .MUXpc_v1(ex_1_muxpc_v1), .MUXpc_v2(ex_1_muxpc_v2));
  Register #(.width(16)) register_16 (
    .D(ex_1_alu_output), .en(1'b1), .Q(register_16_q), .clk(clock_4_out));  // open: clr
  Register #(.width(16)) register_17 (
    .D(ex_1_store_data), .en(1'b1), .Q(register_17_q), .clk(clock_4_out));  // open: clr
  Register #(.width(16)) register_18 (.D(ex_1_pc_2), .en(1'b1), .Q(register_18_q), .clk(clock_4_out));  // open: clr
  Register #(.width(3)) register_19 (.D(ex_1_rt_2), .en(1'b1), .Q(register_19_q), .clk(clock_4_out));  // open: clr
  Register #(.width(3)) register_20 (.D(ex_1_op_2), .en(1'b1), .Q(register_20_q), .clk(clock_4_out));  // open: clr
  Clock clock_4 (.out(clock_4_out));
  MEM mem_1 (
    .RAM_DATA_OUT(memory_mapping_1_data_out), .OP(register_20_q), .rT(register_19_q), .PC(register_18_q),
    .STORE_DATA(register_17_q), .ALU_OUTPUT(register_16_q), .rT_2(mem_1_rt_2),
    .RF_WRITE_DATA(mem_1_rf_write_data), .Bypass_adress(mem_1_bypass_adress),
    .Bypass_value(mem_1_bypass_value), .RAM_DATA_IN(mem_1_ram_data_in), .RAM_ADDR(mem_1_ram_addr),
    .RAM_WE(mem_1_ram_we), .RAM_RE(mem_1_ram_re));
  MEMORY_MAPPING memory_mapping_1 (
    .ADDR(mem_1_ram_addr), .DATA_IN(mem_1_ram_data_in), .WE(mem_1_ram_we), .RE(mem_1_ram_re),
    .DATA_OUT(memory_mapping_1_data_out), .SCREEN_ADRESS(SCREEN_ADRESS), .SCREEN_VALUE(SCREEN_VALUE),
    .SCREEN_ENABLE(SCREEN_ENABLE), .TTY_VALUE(TTY_VALUE), .TTY_ENABLE(TTY_ENABLE),
    .KEYBOARD_VALUE(KEYBOARD_VALUE), .KEYBOARD_ENABLE(KEYBOARD_ENABLE));
  Register #(.width(16)) register_21 (
    .D(mem_1_rf_write_data), .en(1'b1), .Q(register_21_q), .clk(clock_5_out));  // open: clr
  Register #(.width(3)) register_22 (.D(mem_1_rt_2), .en(1'b1), .Q(register_22_q), .clk(clock_5_out));  // open: clr
  Clock clock_5 (.out(clock_5_out));
  WB wb_1 (
    .rT(register_22_q), .RF_WRITE_DATA(register_21_q), .rT_2(undriven),
    .RF_WRITE_DATA_2(wb_1_rf_write_data_2), .WErf(wb_1_werf), .TGT_value(wb_1_tgt_value),
    .TGT_adress(wb_1_tgt_adress));
  Register #(.width(16)) register_23 (
    .D(wb_1_rf_write_data_2), .en(1'b1), .Q(register_23_q), .clk(clock_6_out));  // open: clr
  Register #(.width(3)) register_24 (.D(undriven), .en(1'b1), .Q(register_24_q), .clk(clock_6_out));  // open: clr
  Clock clock_6 (.out(clock_6_out));

  // Notes on the sheet:
  //   PC register return
  //   Bypass return
endmodule

module CTL5 (
  input  [2:0] s1,
  input  [2:0] s2,
  input  [2:0] MEM_adress,
  input  [2:0] WB_adress,
  input  [2:0] END_adress,
  output [1:0] MUXalu2,
  output [1:0] MUXalu2_2
);

  wire comparator_1_eq, comparator_2_eq, comparator_3_eq, comparator_4_eq, comparator_5_eq, comparator_6_eq,
       or_1_out, or_2_out;
  wire [0:0] and_1_out, and_4_out;
  wire [1:1] and_2_out, and_3_out, and_5_out, and_6_out;

  Comparator #(.width(3)) comparator_1 (.a(s1), .b(MEM_adress), .eq(comparator_1_eq));  // open: gt, lt
  Comparator #(.width(3)) comparator_2 (.a(s1), .b(WB_adress), .eq(comparator_2_eq));  // open: gt, lt
  Comparator #(.width(3)) comparator_3 (.a(s1), .b(END_adress), .eq(comparator_3_eq));  // open: gt, lt
  Comparator #(.width(3)) comparator_4 (.a(s2), .b(MEM_adress), .eq(comparator_4_eq));  // open: gt, lt
  Comparator #(.width(3)) comparator_5 (.a(s2), .b(WB_adress), .eq(comparator_5_eq));  // open: gt, lt
  Comparator #(.width(3)) comparator_6 (.a(s2), .b(END_adress), .eq(comparator_6_eq));  // open: gt, lt
  or or_1 (or_1_out, s1[0], s1[1], s1[2]);
  or or_2 (or_2_out, s2[0], s2[1], s2[2]);
  and and_1 (and_1_out[0], or_1_out, comparator_1_eq);
  and and_2 (and_2_out[1], or_1_out, ~comparator_1_eq, comparator_2_eq);  // AND_Gate
  and and_3 (and_3_out[1], or_1_out, ~comparator_1_eq, ~comparator_2_eq, comparator_3_eq);  // AND_Gate
  and and_4 (and_4_out[0], or_2_out, comparator_4_eq);
  and and_5 (and_5_out[1], or_2_out, ~comparator_4_eq, comparator_5_eq);  // AND_Gate
  and and_6 (and_6_out[1], or_2_out, ~comparator_4_eq, ~comparator_5_eq, comparator_6_eq);  // AND_Gate
  assign MUXalu2 = {1'b0, and_1_out[0]} | {and_2_out[1], 1'b0} | {2{and_3_out[1]}};  // OR_Gate or_3, 2 bits wide
  assign MUXalu2_2 = {1'b0, and_4_out[0]} | {and_5_out[1], 1'b0} | {2{and_6_out[1]}};  // OR_Gate or_4, 2 bits wide
endmodule

module MEMORY_MAPPING (
  input  [15:0] ADDR,
  input  [15:0] DATA_IN,
  input  WE,
  input  RE,
  input  [6:0] KEYBOARD_VALUE,
  output [15:0] DATA_OUT,
  output [3:0] SCREEN_ADRESS,
  output [15:0] SCREEN_VALUE,
  output SCREEN_ENABLE,
  output [6:0] TTY_VALUE,
  output TTY_ENABLE,
  output KEYBOARD_ENABLE
);

  wire and_1_out, clock_1_out, KEYBOARD_out, nor_1_out, not_1_out, SCREEN_out, TTY_out;
  wire [15:0] ram_1_data;

  nor nor_1 (nor_1_out, SCREEN_out, TTY_out, KEYBOARD_out);
  and and_1 (and_1_out, WE, nor_1_out);
  not not_1 (not_1_out, clock_1_out);
  Clock clock_1 (.out(clock_1_out));
  and SCREEN (SCREEN_out, ADDR[4], ADDR[5], ADDR[6], ADDR[7], ADDR[8], ADDR[9], ADDR[10], ADDR[11], ADDR[12], ADDR[13], ADDR[14], ADDR[15]);
  and TTY (TTY_out, ADDR[0], ADDR[1], ADDR[2], ADDR[3], ~ADDR[4], ADDR[5], ADDR[6], ADDR[7], ADDR[8], ADDR[9], ADDR[10], ADDR[11], ADDR[12], ADDR[13], ADDR[14], ADDR[15]);  // AND_Gate
  and KEYBOARD (KEYBOARD_out, ~ADDR[0], ~ADDR[1], ~ADDR[2], ~ADDR[3], ~ADDR[4], ADDR[5], ADDR[6], ADDR[7], ADDR[8], ADDR[9], ADDR[10], ADDR[11], ADDR[12], ADDR[13], ADDR[14], ADDR[15]);  // AND_Gate
  RAM #(.addrWidth(16), .dataWidth(16), .bus("separate")) ram_1 (
    .addr(ADDR), .din(DATA_IN), .data(ram_1_data), .str(and_1_out), .sel(1'b1), .clk(not_1_out));  // open: ld, clr
  and and_2 (SCREEN_ENABLE, WE, SCREEN_out);
  and and_3 (TTY_ENABLE, WE, TTY_out);
  and and_4 (KEYBOARD_ENABLE, RE, KEYBOARD_out);
  Multiplexer #(.width(16), .disabled(0), .enable("false")) multiplexer_1 (
    .in0(ram_1_data), .in1({{9{1'b0}}, KEYBOARD_VALUE}), .out(DATA_OUT), .sel(KEYBOARD_ENABLE));

  assign SCREEN_ADRESS = ADDR[3:0];
  assign SCREEN_VALUE = DATA_IN;
  assign TTY_VALUE = DATA_IN[6:0];

  // Notes on the sheet:
  //   KEYBOARD : FFE0
  //   SCREEN : FFF0-FFFF
  //   TTY : FFEF
endmodule

module IN_OUT (
);

  wire keyboard_1_clock, keyboard_1_keyboard_enable_2, pipeline_1_keyboard_enable, pipeline_1_screen_enable,
       pipeline_1_tty_enable, tty_1_tty_clock, tty_1_tty_enable_2;
  wire [3:0] pipeline_1_screen_adress;
  wire [6:0] keyboard_1_keyboard_value_2, keyboard_2_data, pipeline_1_tty_value, tty_1_tty_value_2;
  wire [15:0] pipeline_1_screen_value, screen_1_out_4, screen_1_out_5, screen_1_out_6, screen_1_out_7,
       screen_1_out_8, screen_1_out_9, screen_1_out_10, screen_1_out_11, screen_1_out_12, screen_1_out_13,
       screen_1_out_14, screen_1_out_15, screen_1_out_16, screen_1_out_17, screen_1_out_18, screen_1_out_19;

  PIPELINE pipeline_1 (
    .SCREEN_ADRESS(pipeline_1_screen_adress), .SCREEN_VALUE(pipeline_1_screen_value),
    .SCREEN_ENABLE(pipeline_1_screen_enable), .TTY_VALUE(pipeline_1_tty_value),
    .TTY_ENABLE(pipeline_1_tty_enable), .KEYBOARD_VALUE(keyboard_1_keyboard_value_2),
    .KEYBOARD_ENABLE(pipeline_1_keyboard_enable));
  TTY tty_1 (
    .TTY_VALUE(pipeline_1_tty_value), .TTY_ENABLE(pipeline_1_tty_enable), .TTY_VALUE_2(tty_1_tty_value_2),
    .TTY_CLOCK(tty_1_tty_clock), .TTY_ENABLE_2(tty_1_tty_enable_2));
  KEYBOARD keyboard_1 (
    .KEYBOARD_VALUE_2(keyboard_1_keyboard_value_2), .KEYBOARD_ENABLE(pipeline_1_keyboard_enable),
    .CLOCK(keyboard_1_clock), .KEYBOARD_ENABLE_2(keyboard_1_keyboard_enable_2),
    .KEYBOARD_VALUE(keyboard_2_data));
  DotMatrix #(.inputtype("row"), .matrixcols(16), .matrixrows(16)) dotmatrix_1 (
    .row0(screen_1_out_4), .row1(screen_1_out_5), .row2(screen_1_out_6), .row3(screen_1_out_7),
    .row4(screen_1_out_8), .row5(screen_1_out_9), .row6(screen_1_out_10), .row7(screen_1_out_11),
    .row8(screen_1_out_12), .row9(screen_1_out_13), .row10(screen_1_out_14), .row11(screen_1_out_15),
    .row12(screen_1_out_16), .row13(screen_1_out_17), .row14(screen_1_out_18), .row15(screen_1_out_19));
  SCREEN screen_1 (
    .ADRESS(pipeline_1_screen_adress), .VALUE(pipeline_1_screen_value), .ENABLE(pipeline_1_screen_enable),
    .out_4(screen_1_out_4), .out_5(screen_1_out_5), .out_6(screen_1_out_6), .out_7(screen_1_out_7),
    .out_8(screen_1_out_8), .out_9(screen_1_out_9), .out_10(screen_1_out_10), .out_11(screen_1_out_11),
    .out_12(screen_1_out_12), .out_13(screen_1_out_13), .out_14(screen_1_out_14), .out_15(screen_1_out_15),
    .out_16(screen_1_out_16), .out_17(screen_1_out_17), .out_18(screen_1_out_18), .out_19(screen_1_out_19));
  TTY_part tty_2 (.data(tty_1_tty_value_2), .clk(tty_1_tty_clock), .we(tty_1_tty_enable_2));  // open: clr
  Keyboard keyboard_2 (
    .clk(keyboard_1_clock), .re(keyboard_1_keyboard_enable_2), .data(keyboard_2_data));  // open: clr, avail
endmodule

module SCREEN (
  input  [3:0] ADRESS,
  input  [15:0] VALUE,
  input  ENABLE,
  output [15:0] out_4,
  output [15:0] out_5,
  output [15:0] out_6,
  output [15:0] out_7,
  output [15:0] out_8,
  output [15:0] out_9,
  output [15:0] out_10,
  output [15:0] out_11,
  output [15:0] out_12,
  output [15:0] out_13,
  output [15:0] out_14,
  output [15:0] out_15,
  output [15:0] out_16,
  output [15:0] out_17,
  output [15:0] out_18,
  output [15:0] out_19
);

  wire clock_1_out, demultiplexer_1_out0, demultiplexer_1_out1, demultiplexer_1_out2, demultiplexer_1_out3,
       demultiplexer_1_out4, demultiplexer_1_out5, demultiplexer_1_out6, demultiplexer_1_out7,
       demultiplexer_1_out8, demultiplexer_1_out9, demultiplexer_1_out10, demultiplexer_1_out11,
       demultiplexer_1_out12, demultiplexer_1_out13, demultiplexer_1_out14, demultiplexer_1_out15, not_1_out;

  Demultiplexer #(.select(4), .disabled(0), .enable("false")) demultiplexer_1 (
    .out0(demultiplexer_1_out0), .out1(demultiplexer_1_out1), .out2(demultiplexer_1_out2),
    .out3(demultiplexer_1_out3), .out4(demultiplexer_1_out4), .out5(demultiplexer_1_out5),
    .out6(demultiplexer_1_out6), .out7(demultiplexer_1_out7), .out8(demultiplexer_1_out8),
    .out9(demultiplexer_1_out9), .out10(demultiplexer_1_out10), .out11(demultiplexer_1_out11),
    .out12(demultiplexer_1_out12), .out13(demultiplexer_1_out13), .out14(demultiplexer_1_out14),
    .out15(demultiplexer_1_out15), .in(ENABLE), .sel(ADRESS));
  Clock clock_1 (.out(clock_1_out));
  not not_1 (not_1_out, clock_1_out);
  Register #(.width(16)) register_1 (.D(VALUE), .en(demultiplexer_1_out0), .Q(out_4), .clk(not_1_out));  // open: clr
  Register #(.width(16)) register_2 (.D(VALUE), .en(demultiplexer_1_out1), .Q(out_5), .clk(not_1_out));  // open: clr
  Register #(.width(16)) register_3 (.D(VALUE), .en(demultiplexer_1_out2), .Q(out_6), .clk(not_1_out));  // open: clr
  Register #(.width(16)) register_4 (.D(VALUE), .en(demultiplexer_1_out3), .Q(out_7), .clk(not_1_out));  // open: clr
  Register #(.width(16)) register_5 (.D(VALUE), .en(demultiplexer_1_out4), .Q(out_8), .clk(not_1_out));  // open: clr
  Register #(.width(16)) register_6 (.D(VALUE), .en(demultiplexer_1_out5), .Q(out_9), .clk(not_1_out));  // open: clr
  Register #(.width(16)) register_7 (.D(VALUE), .en(demultiplexer_1_out6), .Q(out_10), .clk(not_1_out));  // open: clr
  Register #(.width(16)) register_8 (.D(VALUE), .en(demultiplexer_1_out7), .Q(out_11), .clk(not_1_out));  // open: clr
  Register #(.width(16)) register_9 (.D(VALUE), .en(demultiplexer_1_out8), .Q(out_12), .clk(not_1_out));  // open: clr
  Register #(.width(16)) register_10 (.D(VALUE), .en(demultiplexer_1_out9), .Q(out_13), .clk(not_1_out));  // open: clr
  Register #(.width(16)) register_11 (.D(VALUE), .en(demultiplexer_1_out10), .Q(out_14), .clk(not_1_out));  // open: clr
  Register #(.width(16)) register_12 (.D(VALUE), .en(demultiplexer_1_out11), .Q(out_15), .clk(not_1_out));  // open: clr
  Register #(.width(16)) register_13 (.D(VALUE), .en(demultiplexer_1_out12), .Q(out_16), .clk(not_1_out));  // open: clr
  Register #(.width(16)) register_14 (.D(VALUE), .en(demultiplexer_1_out13), .Q(out_17), .clk(not_1_out));  // open: clr
  Register #(.width(16)) register_15 (.D(VALUE), .en(demultiplexer_1_out14), .Q(out_18), .clk(not_1_out));  // open: clr
  Register #(.width(16)) register_16 (.D(VALUE), .en(demultiplexer_1_out15), .Q(out_19), .clk(not_1_out));  // open: clr
endmodule

module TTY (
  input  [6:0] TTY_VALUE,
  input  TTY_ENABLE,
  output [6:0] TTY_VALUE_2,
  output TTY_CLOCK,
  output TTY_ENABLE_2
);

  wire clock_1_out;

  not not_1 (TTY_CLOCK, clock_1_out);
  Clock clock_1 (.out(clock_1_out));

  assign TTY_ENABLE_2 = TTY_ENABLE;
  assign TTY_VALUE_2 = TTY_VALUE;
endmodule

module KEYBOARD (
  input  KEYBOARD_ENABLE,
  input  [6:0] KEYBOARD_VALUE,
  output [6:0] KEYBOARD_VALUE_2,
  output CLOCK,
  output KEYBOARD_ENABLE_2
);

  wire clock_1_out, register_1_q;

  Clock clock_1 (.out(clock_1_out));
  not not_1 (CLOCK, clock_1_out);
  Register #(.width(1)) register_1 (.D(KEYBOARD_ENABLE), .en(1'b1), .Q(register_1_q), .clk(CLOCK));  // open: clr
  Register #(.width(1)) register_2 (.D(register_1_q), .Q(KEYBOARD_ENABLE_2), .clk(clock_1_out));  // open: en, clr

  assign KEYBOARD_VALUE_2 = KEYBOARD_VALUE;
endmodule
